// Logisim project ALU.circ as structural Verilog: 3 circuits, main circuit 1bit
module _1bit (
  input  A,
  input  B,
  input  Carry_in,
  input  F0,
  input  F1,
  output out_6,
  output Carry_out
);

  wire and_1_out, and_2_out, and_3_out, and_4_out, and_5_out, and_6_out, and_7_out, FA_out, FB_out, FC_out,
       FD_out, not_1_out, not_2_out, not_3_out, not_4_out, not_5_out, or_1_out, xor_1_out, xor_2_out;

  not not_1 (not_1_out, B);
  and and_1 (and_1_out, A, B);
  or or_1 (or_1_out, A, B);
  not not_2 (not_2_out, F0);
  and FA (FA_out, not_2_out, not_3_out);
  not not_3 (not_3_out, F1);
  not not_4 (not_4_out, F0);
  and FB (FB_out, not_4_out, F1);
  and FC (FC_out, F0, not_5_out);
  not not_5 (not_5_out, F1);
  and FD (FD_out, F0, F1);
  and and_2 (and_2_out, and_1_out, FA_out);
  and and_3 (and_3_out, or_1_out, FB_out);
  and and_4 (and_4_out, not_1_out, FC_out);
  and and_5 (and_5_out, FD_out, B, A);
  or or_2 (Carry_out, and_5_out, and_6_out);
  xor xor_1 (xor_1_out, B, A);
  and and_6 (and_6_out, FD_out, xor_1_out, Carry_in);
  xor xor_2 (xor_2_out, Carry_in, xor_1_out);
  and and_7 (and_7_out, xor_2_out, FD_out);
  or or_3 (out_6, and_2_out, and_3_out, and_4_out, and_7_out);
endmodule

module _8bit (
  input  F0,
  input  F1,
  input  [7:0] A,
  input  [7:0] B,
  input  in_5,
  output [7:0] out_6
);

  wire n1bit_2_carry_out, n1bit_3_carry_out, n1bit_4_carry_out, n1bit_5_carry_out, n1bit_6_carry_out,
       n1bit_7_carry_out, n1bit_8_carry_out;

  _1bit u_1bit_1 (
    .A(A[7]), .B(B[7]), .F0(F0), .F1(F1), .Carry_in(n1bit_2_carry_out), .out_6(out_6[7]));  // open: Carry_out
  _1bit u_1bit_2 (
    .A(A[6]), .B(B[6]), .F0(F0), .F1(F1), .Carry_in(n1bit_4_carry_out), .Carry_out(n1bit_2_carry_out),
    .out_6(out_6[6]));
  _1bit u_1bit_3 (
    .A(A[4]), .B(B[4]), .F0(F0), .F1(F1), .Carry_in(n1bit_5_carry_out), .Carry_out(n1bit_3_carry_out),
    .out_6(out_6[4]));
  _1bit u_1bit_4 (
    .A(A[5]), .B(B[5]), .F0(F0), .F1(F1), .Carry_in(n1bit_3_carry_out), .Carry_out(n1bit_4_carry_out),
    .out_6(out_6[5]));
  _1bit u_1bit_5 (
    .A(A[3]), .B(B[3]), .F0(F0), .F1(F1), .Carry_in(n1bit_6_carry_out), .Carry_out(n1bit_5_carry_out),
    .out_6(out_6[3]));
  _1bit u_1bit_6 (
    .A(A[2]), .B(B[2]), .F0(F0), .F1(F1), .Carry_in(n1bit_7_carry_out), .Carry_out(n1bit_6_carry_out),
    .out_6(out_6[2]));
  _1bit u_1bit_7 (
    .A(A[1]), .B(B[1]), .F0(F0), .F1(F1), .Carry_in(n1bit_8_carry_out), .Carry_out(n1bit_7_carry_out),
    .out_6(out_6[1]));
  _1bit u_1bit_8 (
    .A(A[0]), .B(B[0]), .F0(F0), .F1(F1), .Carry_in(in_5), .Carry_out(n1bit_8_carry_out), .out_6(out_6[0]));
endmodule

module _16bit (
  input  in_1,
  input  in_2,
  input  [15:0] in_3,
  input  [15:0] in_4,
  input  in_5,
  output [15:0] out_6
);

  wire n1bit_2_carry_out, n1bit_3_carry_out, n1bit_4_carry_out, n1bit_5_carry_out, n1bit_6_carry_out,
       n1bit_7_carry_out, n1bit_8_carry_out, n1bit_9_carry_out, n1bit_10_carry_out, n1bit_11_carry_out,
       n1bit_12_carry_out, n1bit_13_carry_out, n1bit_14_carry_out, n1bit_15_carry_out, n1bit_16_carry_out;

  _1bit u_1bit_1 (
    .A(in_3[0]), .B(in_4[0]), .F0(in_1), .F1(in_2), .Carry_in(n1bit_2_carry_out), .out_6(out_6[15]));  // open: Carry_out
  _1bit u_1bit_2 (
    .A(in_3[1]), .B(in_4[1]), .F0(in_1), .F1(in_2), .Carry_in(n1bit_3_carry_out),
    .Carry_out(n1bit_2_carry_out), .out_6(out_6[14]));
  _1bit u_1bit_3 (
    .A(in_3[2]), .B(in_4[2]), .F0(in_1), .F1(in_2), .Carry_in(n1bit_5_carry_out),
    .Carry_out(n1bit_3_carry_out), .out_6(out_6[13]));
  _1bit u_1bit_4 (
    .A(in_3[4]), .B(in_4[4]), .F0(in_1), .F1(in_2), .Carry_in(n1bit_6_carry_out),
    .Carry_out(n1bit_4_carry_out), .out_6(out_6[11]));
  _1bit u_1bit_5 (
    .A(in_3[3]), .B(in_4[3]), .F0(in_1), .F1(in_2), .Carry_in(n1bit_4_carry_out),
    .Carry_out(n1bit_5_carry_out), .out_6(out_6[12]));
  _1bit u_1bit_6 (
    .A(in_3[5]), .B(in_4[5]), .F0(in_1), .F1(in_2), .Carry_in(n1bit_7_carry_out),
    .Carry_out(n1bit_6_carry_out), .out_6(out_6[10]));
  _1bit u_1bit_7 (
    .A(in_3[6]), .B(in_4[6]), .F0(in_1), .F1(in_2), .Carry_in(n1bit_8_carry_out),
    .Carry_out(n1bit_7_carry_out), .out_6(out_6[9]));
  _1bit u_1bit_8 (
    .A(in_3[7]), .B(in_4[7]), .F0(in_1), .F1(in_2), .Carry_in(n1bit_9_carry_out),
    .Carry_out(n1bit_8_carry_out), .out_6(out_6[8]));
  _1bit u_1bit_9 (
    .A(in_3[8]), .B(in_4[8]), .F0(in_1), .F1(in_2), .Carry_in(n1bit_10_carry_out),
    .Carry_out(n1bit_9_carry_out), .out_6(out_6[7]));
  _1bit u_1bit_10 (
    .A(in_3[9]), .B(in_4[9]), .F0(in_1), .F1(in_2), .Carry_in(n1bit_11_carry_out),
    .Carry_out(n1bit_10_carry_out), .out_6(out_6[6]));
  _1bit u_1bit_11 (
    .A(in_3[10]), .B(in_4[10]), .F0(in_1), .F1(in_2), .Carry_in(n1bit_13_carry_out),
    .Carry_out(n1bit_11_carry_out), .out_6(out_6[5]));
  _1bit u_1bit_12 (
    .A(in_3[12]), .B(in_4[12]), .F0(in_1), .F1(in_2), .Carry_in(n1bit_14_carry_out),
    .Carry_out(n1bit_12_carry_out), .out_6(out_6[3]));
  _1bit u_1bit_13 (
    .A(in_3[11]), .B(in_4[11]), .F0(in_1), .F1(in_2), .Carry_in(n1bit_12_carry_out),
    .Carry_out(n1bit_13_carry_out), .out_6(out_6[4]));
  _1bit u_1bit_14 (
    .A(in_3[13]), .B(in_4[13]), .F0(in_1), .F1(in_2), .Carry_in(n1bit_15_carry_out),
    .Carry_out(n1bit_14_carry_out), .out_6(out_6[2]));
  _1bit u_1bit_15 (
    .A(in_3[14]), .B(in_4[14]), .F0(in_1), .F1(in_2), .Carry_in(n1bit_16_carry_out),
    .Carry_out(n1bit_15_carry_out), .out_6(out_6[1]));
  _1bit u_1bit_16 (
    .A(in_3[15]), .B(in_4[15]), .F0(in_1), .F1(in_2), .Carry_in(in_5), .Carry_out(n1bit_16_carry_out),
    .out_6(out_6[0]));
endmodule
