// Logisim project Memory.circ as structural Verilog: 7 circuits, main circuit slot 8 bit
module slot_8_bit (
  input  [7:0] in_1,
  input  in_2,
  output [7:0] out_3
);

  wire clock_1_out;

  Clock clock_1 (.out(clock_1_out));
  D_Flip_Flop d_ff_1 (.clk(clock_1_out), .D(in_1[7]), .Q(out_3[7]), .en(in_2));  // open: Qn, preset, reset
  D_Flip_Flop d_ff_2 (.clk(clock_1_out), .D(in_1[6]), .Q(out_3[6]), .en(in_2));  // open: Qn, preset, reset
  D_Flip_Flop d_ff_3 (.clk(clock_1_out), .D(in_1[5]), .Q(out_3[5]), .en(in_2));  // open: Qn, preset, reset
  D_Flip_Flop d_ff_4 (.clk(clock_1_out), .D(in_1[4]), .Q(out_3[4]), .en(in_2));  // open: Qn, preset, reset
  D_Flip_Flop d_ff_5 (.clk(clock_1_out), .D(in_1[3]), .Q(out_3[3]), .en(in_2));  // open: Qn, preset, reset
  D_Flip_Flop d_ff_6 (.clk(clock_1_out), .D(in_1[2]), .Q(out_3[2]), .en(in_2));  // open: Qn, preset, reset
  D_Flip_Flop d_ff_7 (.clk(clock_1_out), .D(in_1[1]), .Q(out_3[1]), .en(in_2));  // open: Qn, preset, reset
  D_Flip_Flop d_ff_8 (.clk(clock_1_out), .D(in_1[0]), .Q(out_3[0]), .en(in_2));  // open: Qn, preset, reset
endmodule

module bai1 (
  input  NOT,
  input  in_2,
  input  in_3,
  input  in_4,
  input  in_5,
  input  in_6,
  input  in_7,
  input  in_8,
  input  in_9,
  input  in_10,
  output out_11,
  output out_12,
  output out_13,
  output out_14,
  output out_15,
  output out_16
);

  wire nand_2_out, nand_3_out, nand_4_out, nand_5_out, nor_2_out, nor_3_out, nor_4_out, nor_5_out;

  nand nand_1 (out_11, NOT, NOT);
  nand nand_2 (nand_2_out, in_3, in_6);
  nand nand_3 (nand_3_out, in_3, in_6);
  nand nand_4 (nand_4_out, in_8, in_8);
  nand nand_5 (nand_5_out, in_9, in_9);
  nand nand_6 (out_13, nand_2_out, nand_3_out);
  nand nand_7 (out_15, nand_4_out, nand_5_out);
  nor nor_1 (out_12, in_2, in_2);
  nor nor_2 (nor_2_out, in_4, in_4);
  nor nor_3 (nor_3_out, in_5, in_5);
  nor nor_4 (nor_4_out, in_7, in_10);
  nor nor_5 (nor_5_out, in_7, in_10);
  nor nor_6 (out_14, nor_2_out, nor_3_out);
  nor nor_7 (out_16, nor_4_out, nor_5_out);

  // Notes on the sheet:
  //   AND
  //   OR
endmodule

module bai2 (
  input  in_1,
  input  in_2,
  input  in_3,
  input  in_4,
  input  in_5,
  input  in_6,
  input  in_7,
  input  in_8,
  output out_9,
  output out_10,
  output out_11,
  output out_12
);

  wire and_1_out, and_2_out, nand_1_out, nand_2_out, nand_4_out, nand_5_out, not_1_out, not_2_out, not_3_out,
       not_4_out, not_5_out, not_6_out, not_7_out, not_8_out;

  and and_1 (and_1_out, in_1, not_1_out);
  not not_1 (not_1_out, in_3);
  not not_2 (not_2_out, in_1);
  and and_2 (and_2_out, not_2_out, in_3);
  not not_3 (not_3_out, in_8);
  not not_4 (not_4_out, in_5);
  nand nand_1 (nand_1_out, in_5, not_3_out);
  nand nand_2 (nand_2_out, not_4_out, in_8);
  or or_1 (out_9, and_1_out, and_2_out);
  nand nand_3 (out_11, nand_1_out, nand_2_out);
  not not_5 (not_5_out, in_4);
  not not_6 (not_6_out, in_2);
  xor xor_1 (out_12, in_6, in_7);
  nand nand_4 (nand_4_out, in_2, not_5_out);
  nand nand_5 (nand_5_out, not_6_out, in_4);
  not not_7 (not_7_out, nand_4_out);
  not not_8 (not_8_out, nand_5_out);
  or or_2 (out_10, not_7_out, not_8_out);
endmodule

module bai3 (
  input  A,
  input  Select,
  input  B,
  input  in_4,
  input  A_2,
  input  B_2,
  output Multiplexer,
  output A_B,
  output notA_B,
  output A_notB,
  output notA_notB
);

  wire and_1_out, and_2_out, not_1_out, not_2_out, not_3_out;

  not not_1 (not_1_out, A_2);
  and and_1 (and_1_out, A, Select);
  not not_2 (not_2_out, Select);
  and and_2 (and_2_out, not_2_out, B);
  not not_3 (not_3_out, B_2);
  or or_1 (Multiplexer, and_1_out, and_2_out);
  and and_3 (A_B, A_2, in_4, B_2);
  and and_4 (notA_B, not_1_out, in_4, B_2);
  and and_5 (A_notB, A_2, in_4, not_3_out);
  and and_6 (notA_notB, not_1_out, in_4, not_3_out);

  // Notes on the sheet:
  //   Demultiplexer
endmodule

module bai4 (
  input  in_1,
  input  in_2,
  input  in_3,
  output out_4,
  output out_5,
  output out_6,
  output out_7,
  output out_8,
  output out_9,
  output out_10,
  output out_11
);

  wire not_1_out, not_2_out, not_3_out;

  not not_1 (not_1_out, in_1);
  not not_2 (not_2_out, in_2);
  not not_3 (not_3_out, in_3);
  and and_1 (out_4, in_1, in_2, in_3);
  and and_2 (out_5, in_1, in_2, not_3_out);
  and and_3 (out_6, in_1, not_2_out, in_3);
  and and_4 (out_7, not_1_out, in_2, in_3);
  and and_5 (out_8, in_1, not_2_out, not_3_out);
  and and_6 (out_9, not_1_out, in_2, not_3_out);
  and and_7 (out_10, not_1_out, not_2_out, in_3);
  and and_8 (out_11, not_1_out, not_2_out, not_3_out);

  // Notes on the sheet:
  //   Demultiplexer 3 to 8
endmodule

module bai5 (
  input  A,
  input  B,
  output A___B
);

  wire xor_1_out, xor_2_out, xor_3_out, xor_4_out;

  xor xor_1 (xor_1_out, A, B);
  xor xor_2 (xor_2_out, A, B);
  xor xor_3 (xor_3_out, A, B);
  xor xor_4 (xor_4_out, A, B);
  nor nor_1 (A___B, xor_1_out, xor_2_out, xor_3_out, xor_4_out);

  // Notes on the sheet:
  //   Comparator
endmodule

module ram_4_slot (
  input  in_1,
  input  in_2,
  input  [1:0] in_3,
  input  in_4,
  output out_5
);

  wire clock_1_out, d_ff_1_q, d_ff_2_q, d_ff_3_q, d_ff_4_q, demultiplexer_2_out0, demultiplexer_2_out1,
       demultiplexer_2_out2, demultiplexer_2_out3;
  wire [1:0] demultiplexer_1_out0, demultiplexer_1_out1;

  Demultiplexer #(.width(2)) demultiplexer_1 (
    .out0(demultiplexer_1_out0), .out1(demultiplexer_1_out1), .in(in_3), .sel(in_4));  // open: en
  D_Flip_Flop d_ff_1 (.clk(demultiplexer_2_out0), .D(in_1), .Q(d_ff_1_q), .en(in_2));  // open: Qn, preset, reset
  Clock clock_1 (.out(clock_1_out));
  Demultiplexer #(.select(2)) demultiplexer_2 (
    .out0(demultiplexer_2_out0), .out1(demultiplexer_2_out1), .out2(demultiplexer_2_out2),
    .out3(demultiplexer_2_out3), .in(clock_1_out), .sel(demultiplexer_1_out0));  // open: en
  D_Flip_Flop d_ff_2 (.clk(demultiplexer_2_out1), .D(in_1), .Q(d_ff_2_q), .en(in_2));  // open: Qn, preset, reset
  Multiplexer #(.select(2)) multiplexer_1 (
    .in0(d_ff_1_q), .in1(d_ff_2_q), .in2(d_ff_3_q), .in3(d_ff_4_q), .out(out_5), .sel(demultiplexer_1_out1));  // open: en
  D_Flip_Flop d_ff_3 (.clk(demultiplexer_2_out2), .D(in_1), .Q(d_ff_3_q), .en(in_2));  // open: Qn, preset, reset
  D_Flip_Flop d_ff_4 (.clk(demultiplexer_2_out3), .D(in_1), .Q(d_ff_4_q), .en(in_2));  // open: Qn, preset, reset

  // Notes on the sheet:
  //   00
  //   01
  //   10
  //   11
endmodule
