// Logisim project USE AND, OR, XOR, NOT.circ as structural Verilog: 6 circuits, main circuit (A + B) -> C
module A___B_____C (
  input  A,
  input  B,
  input  C,
  output out_4
);

  wire not_1_out, or_1_out;

  or or_1 (or_1_out, A, B);
  not not_1 (not_1_out, or_1_out);
  or or_2 (out_4, not_1_out, C);

  // Notes on the sheet:
  //   (A + B) -> C = not(A + B) + C
endmodule

module A_B__A___C (
  input  B,
  input  A,
  input  C,
  output out_4
);

  wire not_1_out, or_1_out, or_2_out;

  not not_1 (not_1_out, A);
  or or_1 (or_1_out, B, A);
  or or_2 (or_2_out, not_1_out, C);
  and and_1 (out_4, or_1_out, or_2_out);

  // Notes on the sheet:
  //   (A + B)(notA + C)
endmodule

module A___B_C (
  input  in_1,
  input  in_2,
  input  in_3,
  output out_4
);

  wire not_1_out, not_2_out, or_1_out;

  not not_1 (not_1_out, in_1);
  or or_1 (or_1_out, not_1_out, in_2);
  not not_2 (not_2_out, in_3);
  and and_1 (out_4, or_1_out, not_2_out);

  // Notes on the sheet:
  //   (notA + B) notC 
endmodule

module A___B___A_C (
  input  B,
  input  A,
  input  C,
  output out_4
);

  wire not_1_out, not_2_out, not_3_out, or_1_out, or_2_out;

  not not_1 (not_1_out, A);
  not not_2 (not_2_out, C);
  or or_1 (or_1_out, B, not_1_out);
  or or_2 (or_2_out, A, not_2_out);
  not not_3 (not_3_out, or_1_out);
  or or_3 (out_4, not_3_out, or_2_out);

  // Notes on the sheet:
  //   (notA + B)→(A + notC) = not(notA + B) + (A + notC)
endmodule

module AB_BC (
  input  A,
  input  B,
  input  C,
  output out_4
);

  wire and_1_out, and_2_out, not_1_out;

  not not_1 (not_1_out, and_1_out);
  and and_1 (and_1_out, A, B);
  and and_2 (and_2_out, B, C);
  or or_1 (out_4, not_1_out, and_2_out);

  // Notes on the sheet:
  //   AB→BC = not(A . B) + (B . C)
endmodule

module A_B______B_D (
  input  A,
  input  B,
  input  D,
  output out_4
);

  wire not_1_out, or_1_out, or_2_out;

  or or_1 (or_1_out, A, B);
  or or_2 (or_2_out, B, D);
  not not_1 (not_1_out, or_1_out);
  xor xor_1 (out_4, not_1_out, or_2_out);

  // Notes on the sheet:
  //   (not(A + B)) ⨁ (B + D) = (A + B)(B + D) + not(A + B).not(B + D)
endmodule
