// Logisim project USE NAND, NOR, XOR, NOT.circ as structural Verilog: 6 circuits, main circuit (A+B)→C
module A_B__C (
  input  A,
  input  B,
  input  C,
  output out_4
);

  wire nand_1_out, not_1_out, not_2_out, not_3_out;

  not not_1 (not_1_out, A);
  not not_2 (not_2_out, B);
  not not_3 (not_3_out, C);
  nand nand_1 (nand_1_out, not_1_out, not_2_out);
  nand nand_2 (out_4, nand_1_out, not_3_out);

  // Notes on the sheet:
  //   (A+B)→C = not(A+B) + C = (A+B) nand notC = (notA nand notB) nand notC
endmodule

module A_B__A___C (
  input  B,
  input  A,
  input  C,
  output out_4
);

  wire nor_1_out, nor_2_out, not_1_out;

  not not_1 (not_1_out, A);
  nor nor_1 (nor_1_out, B, A);
  nor nor_2 (nor_2_out, not_1_out, C);
  nor nor_3 (out_4, nor_1_out, nor_2_out);

  // Notes on the sheet:
  //   (A+B)(A ̅+C) = not(A+B) nor not(A ̅+C) = (A nor B) nor (notA nor C)
endmodule

module A___B_C (
  input  A,
  input  B,
  input  C,
  output out_4
);

  wire nor_1_out, not_1_out;

  not not_1 (not_1_out, A);
  nor nor_1 (nor_1_out, not_1_out, B);
  nor nor_2 (out_4, nor_1_out, C);

  // Notes on the sheet:
  //   (A ̅+B)C ̅ = not(A ̅+B) nor C = (notA nor B) nor C
endmodule

module A___B___A_C (
  input  B,
  input  A,
  input  C,
  output out_4
);

  wire nand_1_out, nor_1_out, nor_2_out, not_1_out;

  not not_1 (not_1_out, A);
  nor nor_1 (nor_1_out, B, not_1_out);
  nand nand_1 (nand_1_out, not_1_out, C);
  nor nor_2 (nor_2_out, nor_1_out, nand_1_out);
  not not_2 (out_4, nor_2_out);

  // Notes on the sheet:
  //   (A ̅+B)→(A+C ̅) = not(A ̅+B) + (A+C ̅) = not((notA nor B) nor (notA nand C))
endmodule

module AB_BC (
  input  A,
  input  B,
  input  C,
  output out_4
);

  wire nand_1_out, nand_2_out;

  nand nand_1 (nand_1_out, A, B);
  nand nand_2 (nand_2_out, B, C);
  nand nand_3 (out_4, nand_1_out, nand_2_out);

  // Notes on the sheet:
  //   AB→BC = (A nand B) + BC = not(A nand B) nand (B nand C)
endmodule

module A_B______B_D (
  input  A,
  input  B,
  input  D,
  output out_4
);

  wire nor_1_out, nor_2_out, not_1_out;

  nor nor_1 (nor_1_out, A, B);
  not not_1 (not_1_out, nor_2_out);
  nor nor_2 (nor_2_out, B, D);
  xor xor_1 (out_4, nor_1_out, not_1_out);

  // Notes on the sheet:
  //   ((A+B) ̅)⨁(B+D) = (A nor B) xor not(B nor D)
endmodule
