// Logisim project Week10.circ as structural Verilog: 1 circuit, main circuit main
module main (
  input  [15:0] From_C_decoder,
  input  [15:0] From_B_decoder,
  input  [15:0] From_A_decoder,
  output [15:0] To_B_bus,
  output [15:0] To_A_bus,
  output [15:0] Input_from_C_bus
);

  wire clock_1_out;
  wire [15:0] _0_q, A_q, AC_q, AMASK_q, B_q, C_q, d_q, E_q, F_q, IR_q, minus_1_q, PC_q, plus_1_q, SMASK_q,
       SP_q, TIR_q;

  Clock clock_1 (.out(clock_1_out));
  Register #(.width(16)) minus_1 (.D({16{1'b1}}), .Q(minus_1_q), .clk(clock_1_out));  // open: en, clr
  assign To_B_bus = From_B_decoder[7] ? minus_1_q : 16'bz;  // Controlled_Buffer controlled_buffer_1
  assign To_A_bus = From_A_decoder[7] ? minus_1_q : 16'bz;  // Controlled_Buffer controlled_buffer_2
  Register #(.width(16)) F (.D(Input_from_C_bus), .en(From_C_decoder[15]), .Q(F_q), .clk(clock_1_out));  // open: clr
  assign To_B_bus = From_B_decoder[15] ? F_q : 16'bz;  // Controlled_Buffer controlled_buffer_3
  assign To_A_bus = From_A_decoder[15] ? F_q : 16'bz;  // Controlled_Buffer controlled_buffer_4
  Register #(.width(16)) plus_1 (.D(16'h1), .Q(plus_1_q), .clk(clock_1_out));  // open: en, clr
  assign To_B_bus = From_B_decoder[6] ? plus_1_q : 16'bz;  // Controlled_Buffer controlled_buffer_5
  assign To_A_bus = From_A_decoder[6] ? plus_1_q : 16'bz;  // Controlled_Buffer controlled_buffer_6
  Register #(.width(16)) E (.D(Input_from_C_bus), .en(From_C_decoder[14]), .Q(E_q), .clk(clock_1_out));  // open: clr
  assign To_A_bus = From_A_decoder[14] ? E_q : 16'bz;  // Controlled_Buffer controlled_buffer_7
  assign To_B_bus = From_B_decoder[14] ? E_q : 16'bz;  // Controlled_Buffer controlled_buffer_8
  Register #(.width(16)) _0 (.D({16{1'b0}}), .Q(_0_q), .clk(clock_1_out));  // open: en, clr
  assign To_B_bus = From_B_decoder[5] ? _0_q : 16'bz;  // Controlled_Buffer controlled_buffer_9
  assign To_A_bus = From_A_decoder[5] ? _0_q : 16'bz;  // Controlled_Buffer controlled_buffer_10
  Register #(.width(16)) d (.D(Input_from_C_bus), .en(From_C_decoder[13]), .Q(d_q), .clk(clock_1_out));  // open: clr
  assign To_B_bus = From_B_decoder[13] ? d_q : 16'bz;  // Controlled_Buffer controlled_buffer_11
  assign To_A_bus = From_A_decoder[13] ? d_q : 16'bz;  // Controlled_Buffer controlled_buffer_12
  Register #(.width(16)) TIR (.D(Input_from_C_bus), .en(From_C_decoder[4]), .Q(TIR_q));  // open: clk, clr
  assign To_A_bus = From_A_decoder[4] ? TIR_q : 16'bz;  // Controlled_Buffer controlled_buffer_13
  assign To_B_bus = From_B_decoder[4] ? TIR_q : 16'bz;  // Controlled_Buffer controlled_buffer_14
  Register #(.width(16)) C (.D(Input_from_C_bus), .en(From_C_decoder[12]), .Q(C_q));  // open: clk, clr
  assign To_A_bus = From_A_decoder[12] ? C_q : 16'bz;  // Controlled_Buffer controlled_buffer_15
  assign To_B_bus = From_B_decoder[12] ? C_q : 16'bz;  // Controlled_Buffer controlled_buffer_16
  Register #(.width(16)) IR (.D(Input_from_C_bus), .en(From_C_decoder[3]), .Q(IR_q), .clk(clock_1_out));  // open: clr
  assign To_A_bus = From_A_decoder[3] ? IR_q : 16'bz;  // Controlled_Buffer controlled_buffer_17
  assign To_B_bus = From_B_decoder[3] ? IR_q : 16'bz;  // Controlled_Buffer controlled_buffer_18
  Register #(.width(16)) B (.D(Input_from_C_bus), .en(From_C_decoder[11]), .Q(B_q), .clk(clock_1_out));  // open: clr
  assign To_A_bus = From_A_decoder[11] ? B_q : 16'bz;  // Controlled_Buffer controlled_buffer_19
  assign To_B_bus = From_B_decoder[11] ? B_q : 16'bz;  // Controlled_Buffer controlled_buffer_20
  Register #(.width(16)) SP (.D(Input_from_C_bus), .en(From_C_decoder[2]), .Q(SP_q), .clk(clock_1_out));  // open: clr
  assign To_B_bus = From_B_decoder[2] ? SP_q : 16'bz;  // Controlled_Buffer controlled_buffer_21
  assign To_A_bus = From_A_decoder[2] ? SP_q : 16'bz;  // Controlled_Buffer controlled_buffer_22
  Register #(.width(16)) A (.D(Input_from_C_bus), .en(From_C_decoder[10]), .Q(A_q), .clk(clock_1_out));  // open: clr
  assign To_B_bus = From_B_decoder[10] ? A_q : 16'bz;  // Controlled_Buffer controlled_buffer_23
  assign To_A_bus = From_A_decoder[10] ? A_q : 16'bz;  // Controlled_Buffer controlled_buffer_24
  Register #(.width(16)) AC (.D(Input_from_C_bus), .en(From_C_decoder[1]), .Q(AC_q), .clk(clock_1_out));  // open: clr
  assign To_A_bus = From_A_decoder[1] ? AC_q : 16'bz;  // Controlled_Buffer controlled_buffer_25
  assign To_B_bus = From_B_decoder[1] ? AC_q : 16'bz;  // Controlled_Buffer controlled_buffer_26
  Register #(.width(16)) SMASK (.D(16'hff), .Q(SMASK_q), .clk(clock_1_out));  // open: en, clr
  assign To_B_bus = From_B_decoder[9] ? SMASK_q : 16'bz;  // Controlled_Buffer controlled_buffer_27
  assign To_A_bus = From_A_decoder[9] ? SMASK_q : 16'bz;  // Controlled_Buffer controlled_buffer_28
  Register #(.width(16)) PC (.D(Input_from_C_bus), .en(From_C_decoder[0]), .Q(PC_q), .clk(clock_1_out));  // open: clr
  assign To_B_bus = From_B_decoder[0] ? PC_q : 16'bz;  // Controlled_Buffer controlled_buffer_29
  assign To_A_bus = From_A_decoder[0] ? PC_q : 16'bz;  // Controlled_Buffer controlled_buffer_30
  Register #(.width(16)) AMASK (.D(16'hfff), .Q(AMASK_q), .clk(clock_1_out));  // open: en, clr
  assign To_A_bus = From_A_decoder[8] ? AMASK_q : 16'bz;  // Controlled_Buffer controlled_buffer_31
  assign To_B_bus = From_B_decoder[8] ? AMASK_q : 16'bz;  // Controlled_Buffer controlled_buffer_32
endmodule
