// Logisim project Week11.circ as structural Verilog: 2 circuits, main circuit MAR-12bits
module MAR_12bits (
  input  [11:0] Input,
  input  MAR_controller,
  output [11:0] Output
);

  wire Clock_out;

  Clock Clock (.out(Clock_out));
  Register #(.width(12)) register_1 (.D(Input), .en(MAR_controller), .Q(Output), .clk(Clock_out));  // open: clr

  // Notes on the sheet:
  //   Lê Tuấn Anh - 20021286
endmodule

module MBR_16bits (
  input  [15:0] Input__From_main_memory,
  input  RD,
  input  WR,
  input  MBR,
  input  [15:0] Input__Connect_to_C_bus,
  output [15:0] Output,
  output [15:0] Output__to_main_memory
);

  wire and_1_out, and_2_out, Clock_out, not_1_out, not_2_out, not_3_out, or_1_out;
  wire [15:0] controlled_buffer_2_out;

  and and_1 (and_1_out, Clock_out, WR);
  assign Output__to_main_memory = and_1_out ? Output : 16'bz;  // Controlled_Buffer controlled_buffer_1
  assign controlled_buffer_2_out = not_1_out ? Input__From_main_memory : 16'bz;  // Controlled_Buffer controlled_buffer_2
  not not_1 (not_1_out, MBR);
  or or_1 (or_1_out, RD, MBR);
  assign controlled_buffer_2_out = and_2_out ? Input__Connect_to_C_bus : 16'bz;  // Controlled_Buffer controlled_buffer_3
  Clock Clock (.out(Clock_out));
  Register #(.width(16)) register_1 (
    .D(controlled_buffer_2_out), .en(or_1_out), .Q(Output), .clk(Clock_out));  // open: clr
  not not_2 (not_2_out, Clock_out);
  and and_2 (and_2_out, not_2_out, MBR, not_3_out);
  not not_3 (not_3_out, RD);

  // Notes on the sheet:
  //   Lê Tuấn Anh - 20021286
endmodule
