// Logisim project Week12.circ as structural Verilog: 3 circuits, main circuit shifter-16bits
module shifter_16bits (
  input  [15:0] \input ,
  input  [1:0] SH_controller,
  output [15:0] \output 
);

  wire [15:0] shifter_1_out, shifter_2_out;

  Shifter #(.width(16), .shift("lr")) shifter_1 (.in(\input ), .\dist (4'b0001), .out(shifter_1_out));
  Shifter #(.width(16)) shifter_2 (.in(\input ), .\dist (4'b0001), .out(shifter_2_out));
  Multiplexer #(.select(2), .width(16)) multiplexer_1 (
    .in0(\input ), .in1(shifter_1_out), .in2(shifter_2_out), .out(\output ), .sel(SH_controller));  // open: in3, en
endmodule

module Latch_16bits (
  input  [15:0] \input ,
  output [15:0] \output 
);

  wire clock_out;

  Register #(.width(16)) register_1 (.D(\input ), .Q(\output ), .clk(clock_out));  // open: en, clr
  Clock clock (.out(clock_out));
endmodule

module Rotary_shifter_16bits (
  input  [15:0] \input ,
  input  [1:0] SH_controller,
  output [15:0] \output 
);

  wire [15:0] or_1_out, or_2_out, shifter_1_out, shifter_2_out, shifter_3_out, shifter_4_out;

  Shifter #(.width(16), .shift("lr")) shifter_1 (.in(\input ), .\dist (4'b0001), .out(shifter_1_out));
  Shifter #(.width(16)) shifter_2 (.in(\input ), .\dist (4'b1111), .out(shifter_2_out));
  Shifter #(.width(16)) shifter_3 (.in(\input ), .\dist (4'b0001), .out(shifter_3_out));
  Shifter #(.width(16), .shift("lr")) shifter_4 (.in(\input ), .\dist (4'b1111), .out(shifter_4_out));
  assign or_1_out = shifter_1_out | shifter_2_out;  // OR_Gate or_1, 16 bits wide
  assign or_2_out = shifter_3_out | shifter_4_out;  // OR_Gate or_2, 16 bits wide
  Multiplexer #(.select(2), .width(16)) multiplexer_1 (
    .in0(\input ), .in1(or_1_out), .in2(or_2_out), .out(\output ), .sel(SH_controller));  // open: in3, en

  // Notes on the sheet:
  //   A
  //   16-A
endmodule
