// Logisim project Week14.circ as structural Verilog: 3 circuits, main circuit controlStore
module controlStore (
  input  [7:0] _8_bits_Address_binary,
  output [31:0] _32_bits_Output_binary
);

  Hex_Digit_Display hex_digit_display_1 (.value(_8_bits_Address_binary[7:4]));  // open: dp
  Hex_Digit_Display hex_digit_display_2 (.value(_8_bits_Address_binary[3:0]));  // open: dp
  Hex_Digit_Display hex_digit_display_3 (.value(_32_bits_Output_binary[31:28]));  // open: dp
  Hex_Digit_Display hex_digit_display_4 (.value(_32_bits_Output_binary[27:24]));  // open: dp
  Hex_Digit_Display hex_digit_display_5 (.value(_32_bits_Output_binary[23:20]));  // open: dp
  ROM #(.dataWidth(32)) rom_1 (.addr(_8_bits_Address_binary), .data(_32_bits_Output_binary));  // open: sel
  Hex_Digit_Display hex_digit_display_6 (.value(_32_bits_Output_binary[19:16]));  // open: dp
  Hex_Digit_Display hex_digit_display_7 (.value(_32_bits_Output_binary[15:12]));  // open: dp
  Hex_Digit_Display hex_digit_display_8 (.value(_32_bits_Output_binary[11:8]));  // open: dp
  Hex_Digit_Display hex_digit_display_9 (.value(_32_bits_Output_binary[7:4]));  // open: dp
  Hex_Digit_Display hex_digit_display_10 (.value(_32_bits_Output_binary[3:0]));  // open: dp

  // Notes on the sheet:
  //   Control-Store 256x32bits
  //   contents of rom_1 (hex, n*v repeats v):
  //   c00000 506000 b013001c 24143313 3414040b 30000409 c03000 400000 f0110000 11a03100 60200000 3000040f
  //   c03000 400000 e0111000 c03000 516100 981a0000 6011a100 34140419 30000417 30000100 68108300 50000116
  //   60000000 3000041b 68108300 68118300 24143328 34140423 30000421 1a2300 70c0a007 1a2300 71a0a10a
  //   30000426 1a2300 60c0a00d 1a2300 60c0a010 3414042e 3000042c 30000116 60000000 50000100 68108300
  //   34140432 127200 11a02000 68308300 34140441 3414043b 30000438 c01000 527200 60a0200a d22600 400000
  //   60a0200a 3000043e 127200 71a0210a d22600 400000 f0110000 34140449 30000446 d22600 400000 f0100000
  //   101a0100 10110200 70120a00 3000044c 81a9300 6012a200 81a9300 181a0a00 601a6a4b
endmodule

module MIR (
  input  [31:0] in_1,
  input  Clock,
  output out_3,
  output [1:0] out_4,
  output [1:0] out_5,
  output [1:0] out_6,
  output out_7,
  output out_8,
  output out_9,
  output out_10,
  output out_11,
  output [3:0] out_12,
  output [3:0] out_13,
  output [3:0] out_14,
  output [7:0] out_15
);

  Register #(.width(1)) AMUX (.D(in_1[31]), .Q(out_3), .clk(Clock));  // open: en, clr
  Register #(.width(2)) ALU (.D(in_1[28:27]), .Q(out_5), .clk(Clock));  // open: en, clr
  Register #(.width(2)) COND (.D(in_1[30:29]), .Q(out_4), .clk(Clock));  // open: en, clr
  Register #(.width(2)) SH (.D(in_1[26:25]), .Q(out_6), .clk(Clock));  // open: en, clr
  Register #(.width(1)) MBR (.D(in_1[24]), .Q(out_7), .clk(Clock));  // open: en, clr
  Register #(.width(1)) RD (.D(in_1[22]), .Q(out_9), .clk(Clock));  // open: en, clr
  Register #(.width(1)) MAR (.D(in_1[23]), .Q(out_8), .clk(Clock));  // open: en, clr
  Register #(.width(1)) WR (.D(in_1[21]), .Q(out_10), .clk(Clock));  // open: en, clr
  Register #(.width(1)) ENC (.D(in_1[20]), .Q(out_11), .clk(Clock));  // open: en, clr
  Register #(.width(4)) C (.D(in_1[19:16]), .Q(out_12), .clk(Clock));  // open: en, clr
  Register #(.width(4)) B (.D(in_1[15:12]), .Q(out_13), .clk(Clock));  // open: en, clr
  Register #(.width(4)) A (.D(in_1[11:8]), .Q(out_14), .clk(Clock));  // open: en, clr
  Register ADDR (.D(in_1[7:0]), .Q(out_15), .clk(Clock));  // open: en, clr
endmodule

module Micro_Seq (
  input  in_1,
  input  in_2,
  input  [1:0] in_3,
  output out_4
);

  wire and_1_out, and_2_out, and_3_out, not_1_out, not_2_out;

  and and_1 (and_1_out, not_2_out, in_3[0], in_1);
  or or_1 (out_4, and_1_out, and_2_out, and_3_out);
  and and_2 (and_2_out, in_3[1], not_1_out, in_2);
  not not_1 (not_1_out, in_3[0]);
  not not_2 (not_2_out, in_3[1]);
  and and_3 (and_3_out, in_3[0], in_3[1]);
endmodule
