// Logisim project Week5.circ as structural Verilog: 7 circuits, main circuit Bai3
module Bai3 (
  input  [1:0] in_1,
  input  in_2,
  input  Enable,
  input  [15:0] in_4,
  output [15:0] out_5
);

  wire clock_1_out, demultiplexer_1_out0, demultiplexer_1_out1, demultiplexer_1_out2, demultiplexer_1_out3;
  wire [1:0] demultiplexer_2_out0, demultiplexer_2_out1;
  wire [15:0] d_ff_61_q, d_ff_62_q, d_ff_63_q, d_ff_64_q;

  Clock clock_1 (.out(clock_1_out));
  Demultiplexer #(.select(2), .enable("false")) demultiplexer_1 (
    .out0(demultiplexer_1_out0), .out1(demultiplexer_1_out1), .out2(demultiplexer_1_out2),
    .out3(demultiplexer_1_out3), .in(clock_1_out), .sel(demultiplexer_2_out0));
  D_Flip_Flop d_ff_1 (
    .clk(demultiplexer_1_out0), .D(in_4[15]), .Q(d_ff_61_q[15]), .en(Enable));  // open: Qn, preset, reset
  D_Flip_Flop d_ff_2 (
    .clk(demultiplexer_1_out1), .D(in_4[15]), .Q(d_ff_62_q[15]), .en(Enable));  // open: Qn, preset, reset
  D_Flip_Flop d_ff_3 (
    .clk(demultiplexer_1_out2), .D(in_4[15]), .Q(d_ff_63_q[15]), .en(Enable));  // open: Qn, preset, reset
  D_Flip_Flop d_ff_4 (
    .clk(demultiplexer_1_out3), .D(in_4[15]), .Q(d_ff_64_q[15]), .en(Enable));  // open: Qn, preset, reset
  D_Flip_Flop d_ff_5 (
    .clk(demultiplexer_1_out0), .D(in_4[14]), .Q(d_ff_61_q[14]), .en(Enable));  // open: Qn, preset, reset
  D_Flip_Flop d_ff_6 (
    .clk(demultiplexer_1_out1), .D(in_4[14]), .Q(d_ff_62_q[14]), .en(Enable));  // open: Qn, preset, reset
  D_Flip_Flop d_ff_7 (
    .clk(demultiplexer_1_out2), .D(in_4[14]), .Q(d_ff_63_q[14]), .en(Enable));  // open: Qn, preset, reset
  D_Flip_Flop d_ff_8 (
    .clk(demultiplexer_1_out3), .D(in_4[14]), .Q(d_ff_64_q[14]), .en(Enable));  // open: Qn, preset, reset
  D_Flip_Flop d_ff_9 (
    .clk(demultiplexer_1_out0), .D(in_4[13]), .Q(d_ff_61_q[13]), .en(Enable));  // open: Qn, preset, reset
  D_Flip_Flop d_ff_10 (
    .clk(demultiplexer_1_out1), .D(in_4[13]), .Q(d_ff_62_q[13]), .en(Enable));  // open: Qn, preset, reset
  D_Flip_Flop d_ff_11 (
    .clk(demultiplexer_1_out2), .D(in_4[13]), .Q(d_ff_63_q[13]), .en(Enable));  // open: Qn, preset, reset
  D_Flip_Flop d_ff_12 (
    .clk(demultiplexer_1_out3), .D(in_4[13]), .Q(d_ff_64_q[13]), .en(Enable));  // open: Qn, preset, reset
  D_Flip_Flop d_ff_13 (
    .clk(demultiplexer_1_out0), .D(in_4[12]), .Q(d_ff_61_q[12]), .en(Enable));  // open: Qn, preset, reset
  D_Flip_Flop d_ff_14 (
    .clk(demultiplexer_1_out1), .D(in_4[12]), .Q(d_ff_62_q[12]), .en(Enable));  // open: Qn, preset, reset
  D_Flip_Flop d_ff_15 (
    .clk(demultiplexer_1_out2), .D(in_4[12]), .Q(d_ff_63_q[12]), .en(Enable));  // open: Qn, preset, reset
  D_Flip_Flop d_ff_16 (
    .clk(demultiplexer_1_out3), .D(in_4[12]), .Q(d_ff_64_q[12]), .en(Enable));  // open: Qn, preset, reset
  D_Flip_Flop d_ff_17 (
    .clk(demultiplexer_1_out0), .D(in_4[11]), .Q(d_ff_61_q[11]), .en(Enable));  // open: Qn, preset, reset
  D_Flip_Flop d_ff_18 (
    .clk(demultiplexer_1_out1), .D(in_4[11]), .Q(d_ff_62_q[11]), .en(Enable));  // open: Qn, preset, reset
  D_Flip_Flop d_ff_19 (
    .clk(demultiplexer_1_out2), .D(in_4[11]), .Q(d_ff_63_q[11]), .en(Enable));  // open: Qn, preset, reset
  D_Flip_Flop d_ff_20 (
    .clk(demultiplexer_1_out3), .D(in_4[11]), .Q(d_ff_64_q[11]), .en(Enable));  // open: Qn, preset, reset
  D_Flip_Flop d_ff_21 (
    .clk(demultiplexer_1_out0), .D(in_4[10]), .Q(d_ff_61_q[10]), .en(Enable));  // open: Qn, preset, reset
  D_Flip_Flop d_ff_22 (
    .clk(demultiplexer_1_out1), .D(in_4[10]), .Q(d_ff_62_q[10]), .en(Enable));  // open: Qn, preset, reset
  D_Flip_Flop d_ff_23 (
    .clk(demultiplexer_1_out2), .D(in_4[10]), .Q(d_ff_63_q[10]), .en(Enable));  // open: Qn, preset, reset
  D_Flip_Flop d_ff_24 (
    .clk(demultiplexer_1_out3), .D(in_4[10]), .Q(d_ff_64_q[10]), .en(Enable));  // open: Qn, preset, reset
  D_Flip_Flop d_ff_25 (
    .clk(demultiplexer_1_out0), .D(in_4[9]), .Q(d_ff_61_q[9]), .en(Enable));  // open: Qn, preset, reset
  D_Flip_Flop d_ff_26 (
    .clk(demultiplexer_1_out1), .D(in_4[9]), .Q(d_ff_62_q[9]), .en(Enable));  // open: Qn, preset, reset
  D_Flip_Flop d_ff_27 (
    .clk(demultiplexer_1_out2), .D(in_4[9]), .Q(d_ff_63_q[9]), .en(Enable));  // open: Qn, preset, reset
  D_Flip_Flop d_ff_28 (
    .clk(demultiplexer_1_out3), .D(in_4[9]), .Q(d_ff_64_q[9]), .en(Enable));  // open: Qn, preset, reset
  D_Flip_Flop d_ff_29 (
    .clk(demultiplexer_1_out0), .D(in_4[8]), .Q(d_ff_61_q[8]), .en(Enable));  // open: Qn, preset, reset
  D_Flip_Flop d_ff_30 (
    .clk(demultiplexer_1_out1), .D(in_4[8]), .Q(d_ff_62_q[8]), .en(Enable));  // open: Qn, preset, reset
  D_Flip_Flop d_ff_31 (
    .clk(demultiplexer_1_out2), .D(in_4[8]), .Q(d_ff_63_q[8]), .en(Enable));  // open: Qn, preset, reset
  D_Flip_Flop d_ff_32 (
    .clk(demultiplexer_1_out3), .D(in_4[8]), .Q(d_ff_64_q[8]), .en(Enable));  // open: Qn, preset, reset
  Demultiplexer #(.width(2), .enable("false")) demultiplexer_2 (
    .out0(demultiplexer_2_out0), .out1(demultiplexer_2_out1), .in(in_1), .sel(in_2));
  D_Flip_Flop d_ff_33 (
    .clk(demultiplexer_1_out0), .D(in_4[7]), .Q(d_ff_61_q[7]), .en(Enable));  // open: Qn, preset, reset
  D_Flip_Flop d_ff_34 (
    .clk(demultiplexer_1_out1), .D(in_4[7]), .Q(d_ff_62_q[7]), .en(Enable));  // open: Qn, preset, reset
  D_Flip_Flop d_ff_35 (
    .clk(demultiplexer_1_out2), .D(in_4[7]), .Q(d_ff_63_q[7]), .en(Enable));  // open: Qn, preset, reset
  D_Flip_Flop d_ff_36 (
    .clk(demultiplexer_1_out3), .D(in_4[7]), .Q(d_ff_64_q[7]), .en(Enable));  // open: Qn, preset, reset
  D_Flip_Flop d_ff_37 (
    .clk(demultiplexer_1_out0), .D(in_4[6]), .Q(d_ff_61_q[6]), .en(Enable));  // open: Qn, preset, reset
  D_Flip_Flop d_ff_38 (
    .clk(demultiplexer_1_out1), .D(in_4[6]), .Q(d_ff_62_q[6]), .en(Enable));  // open: Qn, preset, reset
  D_Flip_Flop d_ff_39 (
    .clk(demultiplexer_1_out2), .D(in_4[6]), .Q(d_ff_63_q[6]), .en(Enable));  // open: Qn, preset, reset
  D_Flip_Flop d_ff_40 (
    .clk(demultiplexer_1_out3), .D(in_4[6]), .Q(d_ff_64_q[6]), .en(Enable));  // open: Qn, preset, reset
  D_Flip_Flop d_ff_41 (
    .clk(demultiplexer_1_out0), .D(in_4[5]), .Q(d_ff_61_q[5]), .en(Enable));  // open: Qn, preset, reset
  D_Flip_Flop d_ff_42 (
    .clk(demultiplexer_1_out1), .D(in_4[5]), .Q(d_ff_62_q[5]), .en(Enable));  // open: Qn, preset, reset
  D_Flip_Flop d_ff_43 (
    .clk(demultiplexer_1_out2), .D(in_4[5]), .Q(d_ff_63_q[5]), .en(Enable));  // open: Qn, preset, reset
  D_Flip_Flop d_ff_44 (
    .clk(demultiplexer_1_out3), .D(in_4[5]), .Q(d_ff_64_q[5]), .en(Enable));  // open: Qn, preset, reset
  D_Flip_Flop d_ff_45 (
    .clk(demultiplexer_1_out0), .D(in_4[4]), .Q(d_ff_61_q[4]), .en(Enable));  // open: Qn, preset, reset
  D_Flip_Flop d_ff_46 (
    .clk(demultiplexer_1_out1), .D(in_4[4]), .Q(d_ff_62_q[4]), .en(Enable));  // open: Qn, preset, reset
  D_Flip_Flop d_ff_47 (
    .clk(demultiplexer_1_out2), .D(in_4[4]), .Q(d_ff_63_q[4]), .en(Enable));  // open: Qn, preset, reset
  D_Flip_Flop d_ff_48 (
    .clk(demultiplexer_1_out3), .D(in_4[4]), .Q(d_ff_64_q[4]), .en(Enable));  // open: Qn, preset, reset
  D_Flip_Flop d_ff_49 (
    .clk(demultiplexer_1_out0), .D(in_4[3]), .Q(d_ff_61_q[3]), .en(Enable));  // open: Qn, preset, reset
  D_Flip_Flop d_ff_50 (
    .clk(demultiplexer_1_out1), .D(in_4[3]), .Q(d_ff_62_q[3]), .en(Enable));  // open: Qn, preset, reset
  D_Flip_Flop d_ff_51 (
    .clk(demultiplexer_1_out2), .D(in_4[3]), .Q(d_ff_63_q[3]), .en(Enable));  // open: Qn, preset, reset
  D_Flip_Flop d_ff_52 (
    .clk(demultiplexer_1_out3), .D(in_4[3]), .Q(d_ff_64_q[3]), .en(Enable));  // open: Qn, preset, reset
  D_Flip_Flop d_ff_53 (
    .clk(demultiplexer_1_out0), .D(in_4[2]), .Q(d_ff_61_q[2]), .en(Enable));  // open: Qn, preset, reset
  D_Flip_Flop d_ff_54 (
    .clk(demultiplexer_1_out1), .D(in_4[2]), .Q(d_ff_62_q[2]), .en(Enable));  // open: Qn, preset, reset
  D_Flip_Flop d_ff_55 (
    .clk(demultiplexer_1_out2), .D(in_4[2]), .Q(d_ff_63_q[2]), .en(Enable));  // open: Qn, preset, reset
  D_Flip_Flop d_ff_56 (
    .clk(demultiplexer_1_out3), .D(in_4[2]), .Q(d_ff_64_q[2]), .en(Enable));  // open: Qn, preset, reset
  D_Flip_Flop d_ff_57 (
    .clk(demultiplexer_1_out0), .D(in_4[1]), .Q(d_ff_61_q[1]), .en(Enable));  // open: Qn, preset, reset
  D_Flip_Flop d_ff_58 (
    .clk(demultiplexer_1_out1), .D(in_4[1]), .Q(d_ff_62_q[1]), .en(Enable));  // open: Qn, preset, reset
  D_Flip_Flop d_ff_59 (
    .clk(demultiplexer_1_out2), .D(in_4[1]), .Q(d_ff_63_q[1]), .en(Enable));  // open: Qn, preset, reset
  D_Flip_Flop d_ff_60 (
    .clk(demultiplexer_1_out3), .D(in_4[1]), .Q(d_ff_64_q[1]), .en(Enable));  // open: Qn, preset, reset
  D_Flip_Flop d_ff_61 (
    .clk(demultiplexer_1_out0), .D(in_4[0]), .Q(d_ff_61_q[0]), .en(Enable));  // open: Qn, preset, reset
  D_Flip_Flop d_ff_62 (
    .clk(demultiplexer_1_out1), .D(in_4[0]), .Q(d_ff_62_q[0]), .en(Enable));  // open: Qn, preset, reset
  D_Flip_Flop d_ff_63 (
    .clk(demultiplexer_1_out2), .D(in_4[0]), .Q(d_ff_63_q[0]), .en(Enable));  // open: Qn, preset, reset
  D_Flip_Flop d_ff_64 (
    .clk(demultiplexer_1_out3), .D(in_4[0]), .Q(d_ff_64_q[0]), .en(Enable));  // open: Qn, preset, reset
  Multiplexer #(.select(2), .width(16), .enable("false")) multiplexer_1 (
    .in0(d_ff_61_q), .in1(d_ff_62_q), .in2(d_ff_63_q), .in3(d_ff_64_q), .out(out_5),
    .sel(demultiplexer_2_out1));

  // Notes on the sheet:
  //   Input
  //   Output
endmodule

module Bai4 (
  input  cin,
  input  in_2,
  input  B,
  input  A,
  input  [15:0] in_5,
  input  [15:0] in_6,
  input  [15:0] in_7,
  input  [15:0] in_8,
  output [1:0] out_9,
  output [15:0] out_10,
  output [15:0] out_11
);

  wire and_1_out, and_2_out, and_3_out, xor_1_out, xor_2_out;

  xor xor_1 (xor_1_out, in_2, B);
  Adder #(.width(16)) adder_1 (.a(in_5), .b(in_7), .out(out_10));  // open: cin, cout
  xor xor_2 (xor_2_out, cin, xor_1_out);
  and and_1 (and_1_out, A, xor_1_out);
  and and_2 (and_2_out, A, cin);
  and and_3 (and_3_out, xor_1_out, cin);
  xor xor_3 (out_9[0], xor_2_out, A);
  or or_1 (out_9[1], and_1_out, and_2_out, and_3_out);
  Subtractor #(.width(16)) subtractor_1 (.a(in_6), .b(in_8), .out(out_11));  // open: bin, bout

  // Notes on the sheet:
  //   cộng trừ 1 bit
endmodule

module Bai5 (
  input  [7:0] in_1,
  input  in_2,
  output [7:0] out_3
);

  wire and_1_out, and_3_out, and_4_out, and_5_out, and_6_out, and_7_out, and_8_out, and_9_out, and_10_out,
       and_11_out, and_12_out, and_14_out, not_1_out;

  not not_1 (not_1_out, in_2);
  and and_1 (and_1_out, in_1[7], in_2);
  and and_2 (out_3[7], not_1_out, in_1[6]);
  or or_1 (out_3[6], and_1_out, and_5_out);
  and and_3 (and_3_out, in_1[6], in_2);
  and and_4 (and_4_out, in_1[5], in_2);
  and and_5 (and_5_out, not_1_out, in_1[5]);
  or or_2 (out_3[5], and_3_out, and_6_out);
  and and_6 (and_6_out, not_1_out, in_1[4]);
  and and_7 (and_7_out, in_1[4], in_2);
  or or_3 (out_3[4], and_4_out, and_8_out);
  and and_8 (and_8_out, not_1_out, in_1[3]);
  or or_4 (out_3[3], and_7_out, and_11_out);
  and and_9 (and_9_out, in_1[3], in_2);
  and and_10 (and_10_out, in_1[2], in_2);
  and and_11 (and_11_out, not_1_out, in_1[2]);
  or or_5 (out_3[2], and_9_out, and_12_out);
  and and_12 (and_12_out, not_1_out, in_1[1]);
  and and_13 (out_3[0], in_1[1], in_2);
  or or_6 (out_3[1], and_10_out, and_14_out);
  and and_14 (and_14_out, not_1_out, in_1[0]);
endmodule

module Bai6 (
  input  in_1,
  input  in_2,
  input  in_3,
  input  in_4,
  output out_5,
  output out_6,
  output out_7,
  output out_8
);

  nor nor_1 (out_5, in_1, out_7);
  nor nor_2 (out_7, out_5, in_3);
  nand nand_1 (out_6, in_2, out_8);
  nand nand_2 (out_8, out_6, in_4);
endmodule

module Bai7 (
  input  in_1,
  input  in_2,
  output out_3,
  output out_4
);

  wire and_1_out, and_2_out, clock_1_out;

  Clock clock_1 (.out(clock_1_out));
  and and_1 (and_1_out, in_1, clock_1_out);
  and and_2 (and_2_out, clock_1_out, in_2);
  nor nor_1 (out_3, and_1_out, out_4);
  nor nor_2 (out_4, out_3, and_2_out);
endmodule

module Bai8 (
  input  in_1,
  output out_2,
  output out_3
);

  wire and_1_out, and_2_out, clock_1_out, not_1_out;

  Clock clock_1 (.out(clock_1_out));
  not not_1 (not_1_out, in_1);
  and and_1 (and_1_out, in_1, clock_1_out);
  and and_2 (and_2_out, clock_1_out, not_1_out);
  nor nor_1 (out_2, and_1_out, out_3);
  nor nor_2 (out_3, out_2, and_2_out);
endmodule

module Bai9 (
  input  in_1,
  input  in_2,
  input  in_3,
  input  in_4,
  input  in_5,
  output out_6
);

  wire and_1_out, and_2_out, and_3_out, and_4_out, buffer_1_out, buffer_2_out, nand_1_out, nand_2_out,
       nand_3_out, nand_4_out, nand_5_out, not_1_out;

  not not_1 (not_1_out, buffer_1_out);
  buf buffer_1 (buffer_1_out, in_4);
  and and_1 (and_1_out, in_2, in_1);
  and and_2 (and_2_out, in_3, in_4);
  and and_3 (and_3_out, in_3, not_1_out);
  buf buffer_2 (buffer_2_out, in_5);
  and and_4 (and_4_out, and_1_out, and_2_out);
  nand nand_1 (nand_1_out, and_4_out, buffer_2_out);
  nand nand_2 (nand_2_out, and_4_out, nand_1_out);
  nand nand_3 (nand_3_out, nand_2_out, nand_4_out);
  nand nand_4 (nand_4_out, nand_3_out, nand_1_out);
  nand nand_5 (nand_5_out, and_1_out, nand_3_out);
  assign out_6 = and_3_out ? nand_5_out : 1'bz;  // Controlled_Buffer controlled_buffer_1
endmodule
